// Logisim project alu.circ as structural Verilog: 24 circuits, main circuit sll
module main (
  input  [31:0] X,
  input  [31:0] Y,
  input  [3:0] Switch,
  output Signed_Overflow,
  output Equal,
  output [31:0] Result
);

  wire addOverflow;
  wire [31:0] add_1_result, addu_1_result, and_1_result, or_1_result, sll_1_out, slt_1_result, sltu_1_result,
       sra_1_out, srl_1_out, sub_1_out, subu_1_result, xor_1_result;

  srl srl_1 (.X(X), .Y(Y), .Out(srl_1_out));
  SRA sra_1 (.Y(Y), .X(X), .Out(sra_1_out));
  SLL sll_1 (.Y(Y), .X(X), .Out(sll_1_out));
  AND and_1 (.X(X), .Y(Y), .Result(and_1_result));
  OR or_1 (.X(X), .Y(Y), .Result(or_1_result));
  SUBu subu_1 (.X(X), .Y(Y), .Result(subu_1_result));
  SUB sub_1 (.inp1(X), .inp2(Y), .out(sub_1_out));  // open: overflow
  SLT slt_1 (.X(X), .Y(Y), .Result(slt_1_result));
  SLTU sltu_1 (.X(X), .Y(Y), .Result(sltu_1_result));
  ADDu addu_1 (.X(X), .Y(Y), .Result(addu_1_result));
  ADD add_1 (.X(X), .Y(Y), .overflow(addOverflow), .Result(add_1_result));
  XOR xor_1 (.X(X), .Y(Y), .Result(xor_1_result));
  Multiplexer #(.select(4), .width(32)) multiplexer_1 (
    .in0(sll_1_out), .in1(srl_1_out), .in2(sra_1_out), .in3(add_1_result), .in4(addu_1_result),
    .in5(sub_1_out), .in6(subu_1_result), .in7(and_1_result), .in8(or_1_result), .in9(xor_1_result),
    .in10(slt_1_result), .in11(sltu_1_result), .out(Result), .sel(Switch));  // open: in12, in13, in14, in15, en
  Multiplexer #(.select(4)) multiplexer_2 (
    .in0(1'b0), .in1(1'b0), .in2(1'b0), .in3(addOverflow), .in4(1'b0), .in5(1'b0), .in6(1'b0), .in7(1'b0),
    .in8(1'b0), .in9(1'b0), .in10(1'b0), .in11(1'b0), .in12(1'b0), .in13(1'b0), .in14(1'b0), .in15(1'b0),
    .out(Signed_Overflow), .sel(Switch));  // open: en
  Comparator #(.width(32)) comparator_1 (.a(Y), .b(X), .eq(Equal));  // open: gt, lt

  // Other names for the same wires on the sheet: overflow = Signed_Overflow; S[3:0] = Switch

  // Notes on the sheet:
  //   INPUTS to your circuit
  //   SRL
  //   SRA
  //   SLL
  //   AND
  //   OR
  //   SLT
  //   SLTU
  //   DON'T CHANGE THE LOCATIONS OF THE INPUTS AND OUTPUTS!
  //   ADDU
  //   ADD
  //   CHECK IF THERE IS OVERFLOW
  //   OUTPUTS from your circuit
endmodule

module sll (
  input  [31:0] in,
  output [31:0] Out
);


  assign Out = {in[30:0], 1'b0};
endmodule

module slltwo (
  input  [31:0] in,
  output [31:0] Out
);

  wire [31:0] sll_1_out;

  sll sll_1 (.in(in), .Out(sll_1_out));
  sll sll_2 (.in(sll_1_out), .Out(Out));
endmodule

module sllfour (
  input  [31:0] in,
  output [31:0] Out
);

  wire [31:0] slltwo_1_out;

  slltwo slltwo_1 (.in(in), .Out(slltwo_1_out));
  slltwo slltwo_2 (.in(slltwo_1_out), .Out(Out));
endmodule

module sllocho (
  input  [31:0] in,
  output [31:0] Out
);

  wire [31:0] sllfour_1_out;

  sllfour sllfour_1 (.in(in), .Out(sllfour_1_out));
  sllfour sllfour_2 (.in(sllfour_1_out), .Out(Out));
endmodule

module sll16 (
  input  [31:0] in,
  output [31:0] Out
);

  wire [31:0] sllocho_1_out;

  sllocho sllocho_1 (.in(in), .Out(sllocho_1_out));
  sllocho sllocho_2 (.in(sllocho_1_out), .Out(Out));
endmodule

module sll32 (
  input  [31:0] in,
  output [31:0] Out
);

  wire [31:0] sll16_1_out;

  sll16 sll16_1 (.in(in), .Out(sll16_1_out));
  sll16 sll16_2 (.in(sll16_1_out), .Out(Out));
endmodule

module srl (
  input  [31:0] X,
  input  [31:0] Y,
  output [31:0] Out
);

  SLL sll_1 (
    .Y({Y[0], Y[1], Y[2], Y[3], Y[4], Y[5], Y[6], Y[7], Y[8], Y[9], Y[10], Y[11], Y[12], Y[13], Y[14], Y[15], Y[16], Y[17], Y[18], Y[19], Y[20], Y[21], Y[22], Y[23], Y[24], Y[25], Y[26], Y[27], Y[28], Y[29], Y[30], Y[31]}),
    .X(X),
    .Out({Out[0], Out[1], Out[2], Out[3], Out[4], Out[5], Out[6], Out[7], Out[8], Out[9], Out[10], Out[11], Out[12], Out[13], Out[14], Out[15], Out[16], Out[17], Out[18], Out[19], Out[20], Out[21], Out[22], Out[23], Out[24], Out[25], Out[26], Out[27], Out[28], Out[29], Out[30], Out[31]}));
endmodule

module SLL (
  input  [31:0] Y,
  input  [31:0] X,
  output [31:0] Out
);

  wire [31:0] multiplexer_1_out, multiplexer_2_out, multiplexer_3_out, multiplexer_4_out, multiplexer_5_out,
       sll16_1_out, sll32_1_out, sll_1_out, sllfour_1_out, sllocho_1_out, slltwo_1_out;

  sll32 sll32_1 (.in(Y), .Out(sll32_1_out));
  Multiplexer #(.width(32)) multiplexer_1 (
    .in0(Y), .in1(sll32_1_out), .out(multiplexer_1_out), .sel(X[5]));  // open: en
  sll16 sll16_1 (.in(multiplexer_1_out), .Out(sll16_1_out));
  sllfour sllfour_1 (.in(multiplexer_4_out), .Out(sllfour_1_out));
  Multiplexer #(.width(32)) multiplexer_2 (
    .in0(multiplexer_1_out), .in1(sll16_1_out), .out(multiplexer_2_out), .sel(X[4]));  // open: en
  Multiplexer #(.width(32)) multiplexer_3 (
    .in0(multiplexer_4_out), .in1(sllfour_1_out), .out(multiplexer_3_out), .sel(X[2]));  // open: en
  sllocho sllocho_1 (.in(multiplexer_2_out), .Out(sllocho_1_out));
  slltwo slltwo_1 (.in(multiplexer_3_out), .Out(slltwo_1_out));
  Multiplexer #(.width(32)) multiplexer_4 (
    .in0(multiplexer_2_out), .in1(sllocho_1_out), .out(multiplexer_4_out), .sel(X[3]));  // open: en
  Multiplexer #(.width(32)) multiplexer_5 (
    .in0(multiplexer_3_out), .in1(slltwo_1_out), .out(multiplexer_5_out), .sel(X[1]));  // open: en
  sll sll_1 (.in(multiplexer_5_out), .Out(sll_1_out));
  Multiplexer #(.width(32)) multiplexer_6 (
    .in0(multiplexer_5_out), .in1(sll_1_out), .out(Out), .sel(X[0]));  // open: en
endmodule

module sra (
  input  [31:0] Y,
  output [31:0] Out
);


  assign Out = {{2{Y[31]}}, Y[30:1]};
endmodule

module sratwo (
  input  [31:0] in,
  output [31:0] Out
);

  wire [31:0] sra_1_out;

  sra sra_1 (.Y(in), .Out(sra_1_out));
  sra sra_2 (.Y(sra_1_out), .Out(Out));
endmodule

module srafour (
  input  [31:0] in,
  output [31:0] Out
);

  wire [31:0] sratwo_1_out;

  sratwo sratwo_1 (.in(in), .Out(sratwo_1_out));
  sratwo sratwo_2 (.in(sratwo_1_out), .Out(Out));
endmodule

module sraocho (
  input  [31:0] in,
  output [31:0] Out
);

  wire [31:0] srafour_1_out;

  srafour srafour_1 (.in(in), .Out(srafour_1_out));
  srafour srafour_2 (.in(srafour_1_out), .Out(Out));
endmodule

module sra16 (
  input  [31:0] in,
  output [31:0] Out
);

  wire [31:0] sraocho_1_out;

  sraocho sraocho_1 (.in(in), .Out(sraocho_1_out));
  sraocho sraocho_2 (.in(sraocho_1_out), .Out(Out));
endmodule

module SRA (
  input  [31:0] Y,
  input  [31:0] X,
  output [31:0] Out
);

  wire [31:0] multiplexer_1_out, multiplexer_2_out, multiplexer_3_out, multiplexer_4_out, sra16_1_out,
       sra_1_out, srafour_1_out, sraocho_1_out, sratwo_1_out;

  sra16 sra16_1 (.in(Y), .Out(sra16_1_out));
  srafour srafour_1 (.in(multiplexer_3_out), .Out(srafour_1_out));
  Multiplexer #(.width(32)) multiplexer_1 (
    .in0(Y), .in1(sra16_1_out), .out(multiplexer_1_out), .sel(X[4]));  // open: en
  Multiplexer #(.width(32)) multiplexer_2 (
    .in0(multiplexer_3_out), .in1(srafour_1_out), .out(multiplexer_2_out), .sel(X[2]));  // open: en
  sraocho sraocho_1 (.in(multiplexer_1_out), .Out(sraocho_1_out));
  sratwo sratwo_1 (.in(multiplexer_2_out), .Out(sratwo_1_out));
  Multiplexer #(.width(32)) multiplexer_3 (
    .in0(multiplexer_1_out), .in1(sraocho_1_out), .out(multiplexer_3_out), .sel(X[3]));  // open: en
  Multiplexer #(.width(32)) multiplexer_4 (
    .in0(multiplexer_2_out), .in1(sratwo_1_out), .out(multiplexer_4_out), .sel(X[1]));  // open: en
  sra sra_1 (.Y(multiplexer_4_out), .Out(sra_1_out));
  Multiplexer #(.width(32)) multiplexer_5 (
    .in0(multiplexer_4_out), .in1(sra_1_out), .out(Out), .sel(X[0]));  // open: en
endmodule

module ADD (
  input  [31:0] X,
  input  [31:0] Y,
  output overflow,
  output [31:0] Result
);

  wire comparator_1_gt, comparator_2_gt, comparator_3_gt, comparator_4_gt, comparator_5_gt,
       multiplexer_1_out, multiplexer_2_out;
  wire [31:0] adder_1_out, adder_2_out, adder_3_out, adder_4_out, adder_5_out, adder_6_out, adder_7_out,
       adder_8_out, adder_9_out, multiplexer_3_out, not_1_out, not_2_out, not_3_out, not_4_out;
  wire [31:31] multiplexer_4_out;

  assign not_1_out = ~X;  // NOT_Gate not_1, 32 bits wide
  assign not_2_out = ~Y;  // NOT_Gate not_2, 32 bits wide
  Comparator #(.width(1), .mode("unsigned")) comparator_1 (.a(Y[31]), .b(X[31]), .gt(comparator_1_gt));  // open: eq, lt
  assign not_3_out = ~X;  // NOT_Gate not_3, 32 bits wide
  Adder #(.width(32)) adder_1 (.a(not_1_out), .b(32'h1), .out(adder_1_out));  // open: cin, cout
  Adder #(.width(32)) adder_2 (.a(not_2_out), .b(32'h1), .out(adder_2_out));  // open: cin, cout
  assign not_4_out = ~Y;  // NOT_Gate not_4, 32 bits wide
  Comparator #(.width(32), .mode("unsigned")) comparator_2 (
    .a(adder_1_out), .b(Y), .gt(comparator_2_gt));  // open: eq, lt
  Comparator #(.width(32), .mode("unsigned")) comparator_3 (
    .a(X), .b(adder_2_out), .gt(comparator_3_gt));  // open: eq, lt
  Adder #(.width(32)) adder_3 (.a({1'b0, Y[30:0]}), .b({1'b0, X[30:0]}), .out(adder_3_out));  // open: cin, cout
  Adder #(.width(32)) adder_4 (.a({1'b0, X[30:0]}), .b({1'b0, Y[30:0]}), .out(adder_4_out));  // open: cin, cout
  Adder #(.width(32)) adder_5 (.a({1'b0, X[30:0]}), .b({1'b0, Y[30:0]}), .out(adder_5_out));  // open: cin, cout
  Adder #(.width(32)) adder_6 (.a({1'b0, X[30:0]}), .b({1'b0, Y[30:0]}), .out(adder_6_out));  // open: cin, cout
  Adder #(.width(32)) adder_7 (.a(not_3_out), .b(32'h1), .out(adder_7_out));  // open: cin, cout
  Adder #(.width(32)) adder_8 (.a(32'h1), .b(not_4_out), .out(adder_8_out));  // open: cin, cout
  Multiplexer multiplexer_1 (.in0(Y[31]), .in1(X[31]), .out(multiplexer_1_out), .sel(comparator_2_gt));  // open: en
  Multiplexer multiplexer_2 (.in0(X[31]), .in1(Y[31]), .out(multiplexer_2_out), .sel(comparator_3_gt));  // open: en
  Multiplexer #(.width(32)) multiplexer_3 (
    .in0(adder_3_out), .in1(adder_4_out), .out(multiplexer_3_out), .sel(comparator_1_gt));  // open: en
  Comparator #(.width(32), .mode("unsigned")) comparator_4 (
    .a(adder_5_out), .b(32'h7fffffff), .gt(comparator_4_gt));  // open: eq, lt
  Adder #(.width(32)) adder_9 (.a(adder_7_out), .b(adder_8_out), .out(adder_9_out));  // open: cin, cout
  Multiplexer multiplexer_4 (
    .in0(multiplexer_1_out), .in1(multiplexer_2_out), .out(multiplexer_4_out[31]), .sel(comparator_1_gt));  // open: en
  Comparator #(.width(32), .mode("unsigned")) comparator_5 (
    .a(adder_9_out), .b(32'h7fffffff), .gt(comparator_5_gt));  // open: eq, lt
  Multiplexer #(.select(3), .enable("false")) multiplexer_5 (
    .in0(comparator_4_gt), .in1(1'b0), .in2(1'b0), .in3(comparator_5_gt), .out(overflow),
    .sel({1'b0, X[31], Y[31]}));  // open: in4, in5, in6, in7
  Multiplexer #(.select(3), .width(32), .enable("false")) multiplexer_6 (
    .in0(adder_5_out), .in1({multiplexer_4_out[31], multiplexer_3_out[30:0]}),
    .in2({multiplexer_4_out[31], multiplexer_3_out[30:0]}), .in3(adder_6_out), .out(Result),
    .sel({1'b0, X[31], Y[31]}));  // open: in4, in5, in6, in7

  // Notes on the sheet:
  //   SO +/+
  //   +/+
  //   SO -/-
  //   -/-
  //   +/- or -/+
endmodule

module ADDu (
  input  [31:0] X,
  input  [31:0] Y,
  output [31:0] Result
);

  Adder #(.width(32)) adder_1 (.a(X), .b(Y), .out(Result));  // open: cin, cout
endmodule

// SUBU
module SUBu (
  input  [31:0] X,
  input  [31:0] Y,
  output [31:0] Result
);

  Subtractor #(.width(32)) subtractor_1 (.a(X), .b(Y), .out(Result));  // open: bin, bout
endmodule

module AND (
  input  [31:0] X,
  input  [31:0] Y,
  output [31:0] Result
);

  assign Result = X & Y;  // AND_Gate and_1, 32 bits wide
endmodule

module OR (
  input  [31:0] X,
  input  [31:0] Y,
  output [31:0] Result
);

  assign Result = X | Y;  // OR_Gate or_1, 32 bits wide
endmodule

module XOR (
  input  [31:0] X,
  input  [31:0] Y,
  output [31:0] Result
);

  assign Result = X ^ Y;  // XOR_Gate xor_1, 32 bits wide
endmodule

module SLTU (
  input  [31:0] X,
  input  [31:0] Y,
  output [31:0] Result
);

  Comparator #(.width(32), .mode("unsigned")) comparator_1 (.a(X), .b(Y), .lt(Result[0]));  // open: gt, eq

  assign Result[31:1] = {31{1'b0}};
endmodule

module SLT (
  input  [31:0] X,
  input  [31:0] Y,
  output [31:0] Result
);

  Comparator #(.width(32)) comparator_1 (.a(X), .b(Y), .lt(Result[0]));  // open: gt, eq

  assign Result[31:1] = {31{1'b0}};
endmodule

module SUB (
  input  [31:0] inp1,
  input  [31:0] inp2,
  output [31:0] out,
  output overflow
);

  Subtractor #(.width(32)) subtractor_1 (.a(inp1), .b(inp2), .out(out), .bout(overflow));  // open: bin
endmodule
