// Logisim project regfile.circ as structural Verilog: 2 circuits, main circuit main
module main (
  input  [4:0] Read_Register_1,
  input  [4:0] Read_Register_2,
  input  [4:0] Write_Register,
  input  [31:0] Write_Data,
  input  Write_Enable,
  input  Clock,
  output [31:0] s0_Value,
  output [31:0] s1_Value,
  output [31:0] s2_Value,
  output [31:0] ra_Value,
  output [31:0] sp_Value,
  output [31:0] Read_Data_1,
  output [31:0] Read_Data_2
);

  register register_1 (
    .Read_Register_1(Read_Register_1), .Read_Register_2(Read_Register_2), .Write_Register(Write_Register),
    .Write_Data(Write_Data), .Write_Enable(Write_Enable), .Clock(Clock), .s0_Value(s0_Value),
    .s1_Value(s1_Value), .s2_Value(s2_Value), .ra_Value(ra_Value), .sp_Value(sp_Value),
    .Read_Data_1(Read_Data_1), .Read_Data_2(Read_Data_2));

  // Other names for the same wires on the sheet: clk = Clock; read_data1[31:0] = Read_Data_1;
  //   read_data2[31:0] = Read_Data_2; read_reg1[4:0] = Read_Register_1; read_reg2[4:0] = Read_Register_2;
  //   write_en = Write_Enable; write_reg[4:0] = Write_Register

  // Notes on the sheet:
  //   INPUTS to your circuit
  //   DON'T CHANGE THE LOCATIONS OF THE INPUTS AND OUTPUTS!
  //   These are DEBUG/TEST outputs from your circuit.
  //   OUTPUTS from your circuit
endmodule

module register (
  input  [4:0] Read_Register_1,
  input  [4:0] Read_Register_2,
  input  [4:0] Write_Register,
  input  [31:0] Write_Data,
  input  Write_Enable,
  input  Clock,
  output [31:0] Read_Data_1,
  output [31:0] s0_Value,
  output [31:0] s1_Value,
  output [31:0] s2_Value,
  output [31:0] ra_Value,
  output [31:0] sp_Value,
  output [31:0] Read_Data_2
);

  wire decoder_1_out1, decoder_1_out2, decoder_1_out3, decoder_1_out4, decoder_1_out5, decoder_1_out6,
       decoder_1_out7, decoder_1_out8, decoder_1_out9, decoder_1_out10, decoder_1_out11, decoder_1_out12,
       decoder_1_out13, decoder_1_out14, decoder_1_out15, decoder_1_out16, decoder_1_out17, decoder_1_out18,
       decoder_1_out19, decoder_1_out20, decoder_1_out21, decoder_1_out22, decoder_1_out23, decoder_1_out24,
       decoder_1_out25, decoder_1_out26, decoder_1_out27, decoder_1_out28, decoder_1_out29, decoder_1_out30,
       decoder_1_out31;
  wire [31:0] _1_q, _2_q, _3_q, _4_q, _5_q, _6_q, _7_q, _8_q, _9_q, _10_q, _11_q, _12_q, _13_q, _14_q, _15_q,
       _16_q, _20_q, _21_q, _22_q, _23_q, _24_q, _25_q, _28_q, _29_q, _31_q;

  Decoder #(.select(5), .disabled(0)) decoder_1 (
    .out1(decoder_1_out1), .out2(decoder_1_out2), .out3(decoder_1_out3), .out4(decoder_1_out4),
    .out5(decoder_1_out5), .out6(decoder_1_out6), .out7(decoder_1_out7), .out8(decoder_1_out8),
    .out9(decoder_1_out9), .out10(decoder_1_out10), .out11(decoder_1_out11), .out12(decoder_1_out12),
    .out13(decoder_1_out13), .out14(decoder_1_out14), .out15(decoder_1_out15), .out16(decoder_1_out16),
    .out17(decoder_1_out17), .out18(decoder_1_out18), .out19(decoder_1_out19), .out20(decoder_1_out20),
    .out21(decoder_1_out21), .out22(decoder_1_out22), .out23(decoder_1_out23), .out24(decoder_1_out24),
    .out25(decoder_1_out25), .out26(decoder_1_out26), .out27(decoder_1_out27), .out28(decoder_1_out28),
    .out29(decoder_1_out29), .out30(decoder_1_out30), .out31(decoder_1_out31), .sel(Write_Register),
    .en(Write_Enable));  // open: out0
  Register #(.width(32)) _1 (.D(Write_Data), .en(1'b0), .Q(_1_q), .clk(Clock));  // open: clr
  Register #(.width(32)) _2 (.D(Write_Data), .en(decoder_1_out1), .Q(_2_q), .clk(Clock));  // open: clr
  Register #(.width(32)) _3 (.D(Write_Data), .en(decoder_1_out2), .Q(_3_q), .clk(Clock));  // open: clr
  Register #(.width(32)) _4 (.D(Write_Data), .en(decoder_1_out3), .Q(_4_q), .clk(Clock));  // open: clr
  Register #(.width(32)) _5 (.D(Write_Data), .en(decoder_1_out4), .Q(_5_q), .clk(Clock));  // open: clr
  Register #(.width(32)) _6 (.D(Write_Data), .en(decoder_1_out5), .Q(_6_q), .clk(Clock));  // open: clr
  Register #(.width(32)) _7 (.D(Write_Data), .en(decoder_1_out6), .Q(_7_q), .clk(Clock));  // open: clr
  Register #(.width(32)) _8 (.D(Write_Data), .en(decoder_1_out7), .Q(_8_q), .clk(Clock));  // open: clr
  Register #(.width(32)) _9 (.D(Write_Data), .en(decoder_1_out8), .Q(_9_q), .clk(Clock));  // open: clr
  Register #(.width(32)) _10 (.D(Write_Data), .en(decoder_1_out9), .Q(_10_q), .clk(Clock));  // open: clr
  Register #(.width(32)) _11 (.D(Write_Data), .en(decoder_1_out10), .Q(_11_q), .clk(Clock));  // open: clr
  Register #(.width(32)) _12 (.D(Write_Data), .en(decoder_1_out11), .Q(_12_q), .clk(Clock));  // open: clr
  Register #(.width(32)) _13 (.D(Write_Data), .en(decoder_1_out12), .Q(_13_q), .clk(Clock));  // open: clr
  Register #(.width(32)) _14 (.D(Write_Data), .en(decoder_1_out13), .Q(_14_q), .clk(Clock));  // open: clr
  Register #(.width(32)) _15 (.D(Write_Data), .en(decoder_1_out14), .Q(_15_q), .clk(Clock));  // open: clr
  Register #(.width(32)) _16 (.D(Write_Data), .en(decoder_1_out15), .Q(_16_q), .clk(Clock));  // open: clr
  Register #(.width(32)) _17 (.D(Write_Data), .en(decoder_1_out16), .Q(s0_Value), .clk(Clock));  // open: clr
  Register #(.width(32)) _18 (.D(Write_Data), .en(decoder_1_out17), .Q(s1_Value), .clk(Clock));  // open: clr
  Register #(.width(32)) _19 (.D(Write_Data), .en(decoder_1_out18), .Q(s2_Value), .clk(Clock));  // open: clr
  Register #(.width(32)) _20 (.D(Write_Data), .en(decoder_1_out19), .Q(_20_q), .clk(Clock));  // open: clr
  Register #(.width(32)) _21 (.D(Write_Data), .en(decoder_1_out20), .Q(_21_q), .clk(Clock));  // open: clr
  Register #(.width(32)) _22 (.D(Write_Data), .en(decoder_1_out21), .Q(_22_q), .clk(Clock));  // open: clr
  Register #(.width(32)) _23 (.D(Write_Data), .en(decoder_1_out22), .Q(_23_q), .clk(Clock));  // open: clr
  Register #(.width(32)) _24 (.D(Write_Data), .en(decoder_1_out23), .Q(_24_q), .clk(Clock));  // open: clr
  Register #(.width(32)) _25 (.D(Write_Data), .en(decoder_1_out24), .Q(_25_q), .clk(Clock));  // open: clr
  Register #(.width(32)) _26 (.D(Write_Data), .en(decoder_1_out25), .Q(_25_q), .clk(Clock));  // open: clr
  Register #(.width(32)) _27 (.D(Write_Data), .en(decoder_1_out26), .Q(_25_q), .clk(Clock));  // open: clr
  Register #(.width(32)) _28 (.D(Write_Data), .en(decoder_1_out27), .Q(_28_q), .clk(Clock));  // open: clr
  Register #(.width(32)) _29 (.D(Write_Data), .en(decoder_1_out28), .Q(_29_q), .clk(Clock));  // open: clr
  Register #(.width(32)) _30 (.D(Write_Data), .en(decoder_1_out29), .Q(sp_Value), .clk(Clock));  // open: clr
  Register #(.width(32)) _31 (.D(Write_Data), .en(decoder_1_out30), .Q(_31_q), .clk(Clock));  // open: clr
  Register #(.width(32)) _32 (.D(Write_Data), .en(decoder_1_out31), .Q(ra_Value), .clk(Clock));  // open: clr
  Multiplexer #(.select(5), .width(32)) multiplexer_1 (
    .in0(_1_q), .in1(_2_q), .in2(_3_q), .in3(_4_q), .in4(_5_q), .in5(_6_q), .in6(_7_q), .in7(_8_q),
    .in8(_9_q), .in9(_10_q), .in10(_11_q), .in11(_12_q), .in12(_13_q), .in13(_14_q), .in14(_15_q),
    .in15(_16_q), .in16(s0_Value), .in17(s1_Value), .in18(s2_Value), .in19(_20_q), .in20(_21_q),
    .in21(_22_q), .in22(_23_q), .in23(_24_q), .in24(_25_q), .in25(_25_q), .in26(_25_q), .in27(_28_q),
    .in28(_29_q), .in29(sp_Value), .in30(_31_q), .in31(ra_Value), .out(Read_Data_1), .sel(Read_Register_1));  // open: en
  Multiplexer #(.select(5), .width(32)) multiplexer_2 (
    .in0(_1_q), .in1(_2_q), .in2(_3_q), .in3(_4_q), .in4(_5_q), .in5(_6_q), .in6(_7_q), .in7(_8_q),
    .in8(_9_q), .in9(_10_q), .in10(_11_q), .in11(_12_q), .in12(_13_q), .in13(_14_q), .in14(_15_q),
    .in15(_16_q), .in16(s0_Value), .in17(s1_Value), .in18(s2_Value), .in19(_20_q), .in20(_21_q),
    .in21(_22_q), .in22(_23_q), .in23(_24_q), .in24(_25_q), .in25(_25_q), .in26(_25_q), .in27(_28_q),
    .in28(_29_q), .in29(sp_Value), .in30(_31_q), .in31(ra_Value), .out(Read_Data_2), .sel(Read_Register_2));  // open: en

  // Other names for the same wires on the sheet: clk = Clock; read_data1[31:0] = Read_Data_1;
  //   read_data2[31:0] = Read_Data_2; read_reg1[4:0] = Read_Register_1; read_reg2[4:0] = Read_Register_2;
  //   write_en = Write_Enable; write_reg[4:0] = Write_Register

  // Notes on the sheet:
  //   INPUTS to your circuit
  //   These are DEBUG/TEST outputs from your circuit.
endmodule
